// Logisim project core.circ as structural Verilog: 7 circuits, main circuit main
// write data
module regFile (
  input  [2:0] read_reg1,
  input  [2:0] read_reg2,
  input  [2:0] write_reg,
  input  reg_write_en,
  input  [15:0] write_data,
  input  reset,
  input  clk,
  output [15:0] read_data_1,
  output [15:0] read_data_2
);

  wire decoder_1_out0, decoder_1_out1, decoder_1_out2, decoder_1_out3, decoder_1_out4, decoder_1_out5,
       decoder_1_out6, decoder_1_out7;
  wire [15:0] register_1_q, register_2_q, register_3_q, register_4_q, register_5_q, register_6_q,
       register_7_q, register_8_q;

  Decoder #(.select(3)) decoder_1 (
    .out0(decoder_1_out0), .out1(decoder_1_out1), .out2(decoder_1_out2), .out3(decoder_1_out3),
    .out4(decoder_1_out4), .out5(decoder_1_out5), .out6(decoder_1_out6), .out7(decoder_1_out7),
    .sel(write_reg), .en(reg_write_en));
  Register #(.width(16)) register_1 (.D({16{1'b0}}), .en(decoder_1_out0), .clk(clk), .Q(register_1_q), .clr(reset));
  Register #(.width(16)) register_2 (.D(write_data), .en(decoder_1_out1), .clk(clk), .Q(register_2_q), .clr(reset));
  Register #(.width(16)) register_3 (.D(write_data), .en(decoder_1_out2), .clk(clk), .Q(register_3_q), .clr(reset));
  Register #(.width(16)) register_4 (.D(write_data), .en(decoder_1_out3), .clk(clk), .Q(register_4_q), .clr(reset));
  Register #(.width(16)) register_5 (.D(write_data), .en(decoder_1_out4), .clk(clk), .Q(register_5_q), .clr(reset));
  Register #(.width(16)) register_6 (.D(write_data), .en(decoder_1_out5), .clk(clk), .Q(register_6_q), .clr(reset));
  Register #(.width(16)) register_7 (.D(write_data), .en(decoder_1_out6), .clk(clk), .Q(register_7_q), .clr(reset));
  Register #(.width(16)) register_8 (.D(write_data), .en(decoder_1_out7), .clk(clk), .Q(register_8_q), .clr(reset));
  // Probe on register_1_q
  // Probe on register_2_q
  // Probe on register_3_q
  // Probe on register_4_q
  // Probe on register_5_q
  // Probe on register_6_q
  // Probe on register_7_q
  // Probe on register_8_q
  Multiplexer #(.select(3), .width(16)) multiplexer_1 (
    .in0(register_1_q), .in1(register_2_q), .in2(register_3_q), .in3(register_4_q), .in4(register_5_q),
    .in5(register_6_q), .in6(register_7_q), .in7(register_8_q), .out(read_data_1), .sel(read_reg1));
  Multiplexer #(.select(3), .width(16)) multiplexer_2 (
    .in0(register_1_q), .in1(register_2_q), .in2(register_3_q), .in3(register_4_q), .in4(register_5_q),
    .in5(register_6_q), .in6(register_7_q), .in7(register_8_q), .out(read_data_2), .sel(read_reg2));
endmodule

module main (
  input  reset
);

  wire bit_extender_1_out, clk_out, control_unit_1_beq, control_unit_1_beqz, control_unit_1_i_alu_we,
       control_unit_1_j_type_en, control_unit_1_jal, control_unit_1_jr, control_unit_1_k_input,
       control_unit_1_lw, control_unit_1_r_alu_we, control_unit_1_sw, control_unit_1_tty_output,
       multiplexer_7_out, or_1_out, pc_i_logic_1_pc_i_mux;
  wire [2:0] control_unit_1_i_rd, control_unit_1_i_rs, control_unit_1_r_op_type, control_unit_1_r_rd,
       control_unit_1_r_rs, control_unit_1_r_rt, multiplexer_3_out, multiplexer_4_out, multiplexer_5_out,
       multiplexer_8_out;
  wire [3:0] control_unit_1_op_code;
  wire [5:0] control_unit_1_immediate;
  wire [6:0] bit_extender_2_out, keyboard_1_data;
  wire [11:0] control_unit_1_address;
  wire [15:0] adder_1_out, adder_2_out, alu_1_i_alu_output, alu_1_r_alu_output, DMEM_dout, IMEM_data,
       multiplexer_1_out, multiplexer_2_out, multiplexer_6_out, multiplexer_9_out, multiplexer_10_out,
       multiplexer_11_out, multiplexer_12_out, multiplexer_13_out, pc_i_logic_1_pc_beqz, pc_j_logic_1_pc_o,
       PC_q, regfile_1_read_data_1, regfile_1_read_data_2, sign_extender_1_extended_o;

  // Probe on multiplexer_6_out
  Clock clk (.out(clk_out));
  Register #(.width(16)) PC (.D(multiplexer_6_out), .clk(clk_out), .Q(PC_q), .clr(reset));  // open: en
  ROM #(.addrWidth(16), .dataWidth(16)) IMEM (.addr(PC_q), .data(IMEM_data));
  Adder #(.width(16)) adder_1 (.a(16'h1), .b(PC_q), .out(adder_1_out));  // open: cin, cout
  Multiplexer #(.width(16)) multiplexer_1 (
    .in0(adder_1_out), .in1(alu_1_i_alu_output), .out(multiplexer_1_out), .sel(control_unit_1_jr));
  PC_I_logic pc_i_logic_1 (
    .immediate(sign_extender_1_extended_o), .PC(multiplexer_1_out), .beqz(control_unit_1_beqz),
    .beqz_I(bit_extender_1_out), .beq(control_unit_1_beq), .rd(regfile_1_read_data_2),
    .rs(regfile_1_read_data_1), .PC_beqz(pc_i_logic_1_pc_beqz), .PC_I_MUX(pc_i_logic_1_pc_i_mux));
  Bit_Extender #(.in_width(16), .out_width(1)) bit_extender_1 (.in(alu_1_i_alu_output), .out(bit_extender_1_out));
  Multiplexer #(.width(16)) multiplexer_2 (
    .in0(multiplexer_1_out), .in1(pc_i_logic_1_pc_beqz), .out(multiplexer_2_out), .sel(pc_i_logic_1_pc_i_mux));
  Multiplexer #(.width(3)) multiplexer_3 (
    .in0(control_unit_1_r_rt), .in1(control_unit_1_i_rd), .out(multiplexer_3_out), .sel(control_unit_1_beq));
  control_unit control_unit_1 (
    .instruction(IMEM_data), .R_op_type(control_unit_1_r_op_type), .R_rd(control_unit_1_r_rd),
    .R_rt(control_unit_1_r_rt), .R_rs(control_unit_1_r_rs), .I_rd(control_unit_1_i_rd),
    .I_rs(control_unit_1_i_rs), .immediate(control_unit_1_immediate), .address(control_unit_1_address),
    .R_ALU_WE(control_unit_1_r_alu_we), .I_ALU_WE(control_unit_1_i_alu_we), .op_code(control_unit_1_op_code),
    .lw(control_unit_1_lw), .sw(control_unit_1_sw), .k_input(control_unit_1_k_input),
    .tty_output(control_unit_1_tty_output), .beq(control_unit_1_beq), .beqz(control_unit_1_beqz),
    .jr(control_unit_1_jr), .jal(control_unit_1_jal), .J_TYPE_EN(control_unit_1_j_type_en));  // open: addi, subi, andi, ori, addiu, subiu, j
  PC_J_logic pc_j_logic_1 (.addr(control_unit_1_address), .PC(multiplexer_2_out), .PC_o(pc_j_logic_1_pc_o));
  Multiplexer #(.width(3)) multiplexer_4 (
    .in0(control_unit_1_i_rd), .in1(control_unit_1_r_rd), .out(multiplexer_4_out),
    .sel(control_unit_1_r_alu_we));
  Multiplexer #(.width(3)) multiplexer_5 (
    .in0(control_unit_1_i_rs), .in1(control_unit_1_r_rs), .out(multiplexer_5_out),
    .sel(control_unit_1_r_alu_we));
  Multiplexer #(.width(16)) multiplexer_6 (
    .in0(multiplexer_2_out), .in1(pc_j_logic_1_pc_o), .out(multiplexer_6_out), .sel(control_unit_1_j_type_en));
  Multiplexer multiplexer_7 (
    .in0(or_1_out), .in1(control_unit_1_jal), .out(multiplexer_7_out), .sel(control_unit_1_jal));
  or or_1 (or_1_out, control_unit_1_r_alu_we, control_unit_1_i_alu_we);
  Multiplexer #(.width(3)) multiplexer_8 (
    .in0(multiplexer_4_out), .in1(3'b111), .out(multiplexer_8_out), .sel(control_unit_1_jal));
  // Probe on multiplexer_8_out
  Multiplexer #(.width(16)) multiplexer_9 (
    .in0(multiplexer_10_out), .in1(multiplexer_2_out), .out(multiplexer_9_out), .sel(control_unit_1_jal));
  Multiplexer #(.width(16)) multiplexer_10 (
    .in0(multiplexer_13_out), .in1(sign_extender_1_extended_o), .out(multiplexer_10_out),
    .sel(control_unit_1_k_input));
  Keyboard keyboard_1 (.clk(clk_out), .re(control_unit_1_k_input), .clr(reset), .data(keyboard_1_data));  // open: avail
  regFile regfile_1 (
    .read_reg1(multiplexer_5_out), .read_reg2(multiplexer_3_out), .write_reg(multiplexer_8_out),
    .reg_write_en(multiplexer_7_out), .write_data(multiplexer_9_out), .reset(reset), .clk(clk_out),
    .read_data_1(regfile_1_read_data_1), .read_data_2(regfile_1_read_data_2));
  Multiplexer #(.width(16)) multiplexer_11 (
    .in0(regfile_1_read_data_2), .in1(sign_extender_1_extended_o), .out(multiplexer_11_out),
    .sel(control_unit_1_i_alu_we));
  sign_extender sign_extender_1 (
    .immediate(control_unit_1_immediate), .op_code(control_unit_1_op_code), .keyboard(keyboard_1_data),
    .extended_o(sign_extender_1_extended_o));
  // Probe on keyboard_1_data
  // Probe on bit_extender_2_out
  Bit_Extender #(.in_width(16), .out_width(7), .\type ("zero")) bit_extender_2 (
    .in(alu_1_i_alu_output), .out(bit_extender_2_out));
  // Probe on multiplexer_9_out
  TTY #(.trigger("falling")) tty_1 (
    .data(bit_extender_2_out), .clk(clk_out), .we(control_unit_1_tty_output), .clr(reset));
  ALU alu_1 (
    .A(regfile_1_read_data_1), .B(multiplexer_11_out), .op_type(control_unit_1_r_op_type),
    .op_code(control_unit_1_op_code), .R_ALU_output(alu_1_r_alu_output), .I_ALU_output(alu_1_i_alu_output));
  // Probe on multiplexer_13_out
  Adder #(.width(16)) adder_2 (
    .a(regfile_1_read_data_1), .b(sign_extender_1_extended_o), .out(adder_2_out));  // open: cin, cout
  // Probe on regfile_1_read_data_2
  RAM #(.addrWidth(16), .asyncread("true"), .dataWidth(16)) DMEM (
    .addr(adder_2_out), .we(control_unit_1_sw), .clk(clk_out), .din(regfile_1_read_data_2), .dout(DMEM_dout));  // open: oe
  // Probe on DMEM_dout
  Multiplexer #(.width(16)) multiplexer_12 (
    .in0(alu_1_i_alu_output), .in1(DMEM_dout), .out(multiplexer_12_out), .sel(control_unit_1_lw));
  Multiplexer #(.width(16)) multiplexer_13 (
    .in0(multiplexer_12_out), .in1(alu_1_r_alu_output), .out(multiplexer_13_out),
    .sel(control_unit_1_r_alu_we));

  // Notes on the sheet:
  //   contents of IMEM (hex, n*v repeats v):
  //   1245 e003 f00e c207 290 2241 f003 16c1 1910 1b42 b70d 75c f00a de00 b6c 75c a600
endmodule

module ALU (
  input  [15:0] A,
  input  [15:0] B,
  input  [2:0] op_type,
  input  [3:0] op_code,
  output [15:0] R_ALU_output,
  output [15:0] I_ALU_output
);

  wire comparator_1_lt, comparator_2_eq;
  wire [3:0] bit_extender_1_out;
  wire [15:0] adder_1_out, and_1_out, bit_extender_2_out, bit_extender_3_out, multiplier_1_out, not_1_out,
       or_1_out, shifter_1_out, subtractor_1_out;

  Bit_Extender #(.in_width(16), .out_width(4), .\type ("zero")) bit_extender_1 (.in(B), .out(bit_extender_1_out));
  assign not_1_out = ~A;  // NOT_Gate not_1, 16 bits wide
  Adder #(.width(16)) adder_1 (.a(A), .b(B), .out(adder_1_out));  // open: cin, cout
  Subtractor #(.width(16)) subtractor_1 (.a(A), .b(B), .out(subtractor_1_out));  // open: bin, bout
  Comparator #(.width(16)) comparator_1 (.a(A), .b(B), .lt(comparator_1_lt));  // open: gt, eq
  assign bit_extender_2_out = {{15{1'b0}}, comparator_1_lt};  // Bit_Extender bit_extender_2
  Shifter #(.shift("ar"), .width(16)) shifter_1 (.in(A), .\dist (bit_extender_1_out), .out(shifter_1_out));
  Multiplier #(.width(16)) multiplier_1 (.a(A), .b(B), .out(multiplier_1_out));  // open: cin, cout
  assign and_1_out = A & B;  // AND_Gate and_1, 16 bits wide
  assign or_1_out = A | B;  // OR_Gate or_1, 16 bits wide
  assign bit_extender_3_out = {{15{comparator_2_eq}}, comparator_2_eq};  // Bit_Extender bit_extender_3
  Comparator #(.mode("unsigned"), .width(16)) comparator_2 (
    .a(A), .b({16{1'b0}}), .eq(comparator_2_eq));  // open: gt, lt
  Multiplexer #(.select(3), .width(16)) multiplexer_1 (
    .in0(adder_1_out), .in1(subtractor_1_out), .in2(bit_extender_2_out), .in3(shifter_1_out),
    .in4(multiplier_1_out), .in5(and_1_out), .in6(or_1_out), .in7(not_1_out), .out(R_ALU_output),
    .sel(op_type));
  Multiplexer #(.select(4), .width(16)) multiplexer_2 (
    .in0({16{1'b0}}), .in1(adder_1_out), .in2(subtractor_1_out), .in3(and_1_out), .in4(or_1_out),
    .in5(adder_1_out), .in6(subtractor_1_out), .in7(adder_1_out), .in8(adder_1_out), .in9(B), .in10(A),
    .in11({16{1'b0}}), .in12(bit_extender_3_out), .in13(A), .in14({16{1'b0}}), .in15({16{1'b0}}),
    .out(I_ALU_output), .sel(op_code));

  // Notes on the sheet:
  //   add
  //   sub
  //   slt
  //   sra
  //   mul
  //   and
  //   or
  //   not
endmodule

module control_unit (
  input  [15:0] instruction,
  output [2:0] R_op_type,
  output [2:0] R_rd,
  output [2:0] R_rt,
  output [2:0] R_rs,
  output [2:0] I_rd,
  output [2:0] I_rs,
  output [5:0] immediate,
  output [11:0] address,
  output R_ALU_WE,
  output I_ALU_WE,
  output [3:0] op_code,
  output addi,
  output subi,
  output andi,
  output ori,
  output addiu,
  output subiu,
  output lw,
  output sw,
  output k_input,
  output tty_output,
  output beq,
  output beqz,
  output jr,
  output jal,
  output j,
  output J_TYPE_EN
);

  Decoder #(.select(4)) decoder_1 (
    .out0(R_ALU_WE), .out1(addi), .out2(subi), .out3(andi), .out4(ori), .out5(addiu), .out6(subiu),
    .out7(lw), .out8(sw), .out9(k_input), .out10(tty_output), .out11(beq), .out12(beqz), .out13(jr),
    .out14(jal), .out15(j), .sel(instruction[15:12]));  // open: en
  or or_1 (J_TYPE_EN, jal, j);
  or or_2 (I_ALU_WE, addi, subi, andi, ori, addiu, subiu, lw, 1'b0, k_input, 1'b0, 1'b0, 1'b0, 1'b0);

  assign address = instruction[11:0];
  assign I_rd = instruction[8:6];
  assign I_rs = instruction[11:9];
  assign immediate = instruction[5:0];
  assign op_code = instruction[15:12];
  assign R_op_type = instruction[2:0];
  assign R_rd = instruction[5:3];
  assign R_rs = instruction[11:9];
  assign R_rt = instruction[8:6];
endmodule

module sign_extender (
  input  [5:0] immediate,
  input  [3:0] op_code,
  input  [6:0] keyboard,
  output [15:0] extended_o
);

  wire [15:0] bit_extender_1_out, bit_extender_2_out, bit_extender_3_out;

  assign bit_extender_1_out = {{9{1'b0}}, keyboard};  // Bit_Extender bit_extender_1
  assign bit_extender_2_out = {{10{immediate[5]}}, immediate};  // Bit_Extender bit_extender_2
  assign bit_extender_3_out = {{10{1'b0}}, immediate};  // Bit_Extender bit_extender_3
  Multiplexer #(.select(4), .width(16)) multiplexer_1 (
    .in0({16{1'b0}}), .in1(bit_extender_2_out), .in2(bit_extender_2_out), .in3(bit_extender_3_out),
    .in4(bit_extender_3_out), .in5(bit_extender_3_out), .in6(bit_extender_3_out), .in7(bit_extender_3_out),
    .in8(bit_extender_3_out), .in9(bit_extender_1_out), .in10({16{1'b0}}), .in11(bit_extender_3_out),
    .in12(bit_extender_3_out), .in13({16{1'b0}}), .in14({16{1'b0}}), .in15({16{1'b0}}), .out(extended_o),
    .sel(op_code));
endmodule

module PC_I_logic (
  input  [15:0] immediate,
  input  [15:0] PC,
  input  beqz,
  input  beqz_I,
  input  beq,
  input  [15:0] rd,
  input  [15:0] rs,
  output [15:0] PC_beqz,
  output PC_I_MUX
);

  wire and_1_out, and_2_out, comparator_1_eq;

  Comparator #(.mode("unsigned"), .width(16)) comparator_1 (.a(rd), .b(rs), .eq(comparator_1_eq));  // open: gt, lt
  and and_1 (and_1_out, beqz, beqz_I);
  and and_2 (and_2_out, beq, comparator_1_eq);
  or or_1 (PC_I_MUX, and_1_out, and_2_out);

  assign PC_beqz = {PC[15:6], immediate[5:0]};
endmodule

module PC_J_logic (
  input  [11:0] addr,
  input  [15:0] PC,
  output [15:0] PC_o
);


  assign PC_o = {PC[15:12], addr};
endmodule
